# Fritzing sketch PlantDiagram (saved by Fritzing 0.9.3b)
perfboards: 1

parts:
  LCD1 = LCD screen
  Part1 = Arduino Uno (Rev3)
  R1 = Rotary Potentiometer (Small) [maximum_resistance=100kΩ package=THT]
  R2 = Resistor [tolerance=±5% resistance=220 package=THT]

nets:
  VSS: LCD1.VSS, LCD1.LED-, Part1.GND, R1.leg2
  VDD: LCD1.VDD, LCD1.R/W, Part1.5V, R1.leg1, R2.Pin_0
  N1: LCD1.V0, R1.wiper
  N2: LCD1.RS, Part1.D12/MISO
  N3: LCD1.E, Part1.D11_PWM/MOSI
  N4: LCD1.DB4, Part1.D5_PWM
  N5: LCD1.DB5, Part1.D4
  N6: LCD1.DB6, Part1.D3_PWM
  N7: LCD1.DB7, Part1.D2
  N8: LCD1.LED+, R2.Pin_1

// code stored in the sketch: sketch_aug07a.ino
// MODULES
#include <LiquidCrystal.h>
#include <math.h>

// Initaite Pins
int pinOut = 8; // Relay
int sensor_pin = A0; // Moisture sensor
int output_value ; // Moisture sensor

// Create a custom value for the LCD screen
const int rs = 12, en = 11, d4 = 5, d5 = 4, d6 = 3, d7 = 2;
LiquidCrystal lcd(rs, en, d4, d5, d6, d7);
uint8_t testChar[8] = {0xff,0xff,0xff,0xff,0xff,0xff,0xff,0xff}; // Custom character

// This will be use for the loading bar
int lodval = 0;


// Setup Function
void setup() {
  Serial.begin(9600);
  Serial.println("starting");

  
  pinMode(pinOut, OUTPUT); // Relay
  lcd.begin(16, 2); // Custom character
  lcd.createChar(0, testChar); // Sends the custom char to lcd
  // Following is all just Printing to LCD
  lcd.setCursor(0, 0);
  lcd.print("Starting");
  lcd.setCursor(7, 1);
  lcd.print("Program");
  delay(5000);
  lcd.setCursor(0,0);
  lcd.print("Moisture:");
  lcd.setCursor(15,0);
  lcd.print("%");
  lcd.setCursor(7, 1);
  lcd.print("       ");
  // Prints End
  
}

// Reads the moisture level
int moist_read(){
  output_value = analogRead(sensor_pin);
  output_value = map(output_value,550,0,0,100);
  int moist = (100 - output_value);
  if (moist > 100){
    lodval = 0;
    return 100;
  } else if (moist < 5){
    lodval = lodval + 1;
    return 0;
  } else {
    lodval = 0;
    return moist;
  }
}

// turns on the Pump
void pump_on(){
  digitalWrite(pinOut, HIGH);
  delay(15000);
  digitalWrite(pinOut, LOW);
  lodval = -1;
}

// Loading Bar function
int loading(){
  int tfbool;
  
  if(lodval == 0){
    lcd.setCursor(0,1);
    lcd.print("                ");
    tfbool =  false;
  } else if(lodval == 16){
    lcd.setCursor(lodval - 1, 1);
    lodval = 1;
    lcd.print(char(0));
    tfbool = true;
  } else{
    lcd.setCursor(lodval - 1, 1);
    lcd.print(char(0));
    tfbool =  false;
  }
  delay(1000);
  return tfbool;
}


// LCD printing function
int LCDprint(){
  lcd.setCursor(11,0);
  lcd.print("   ");
  lcd.setCursor(11,0);
  int mst_val = moist_read();
  lcd.print(mst_val);
  int bol = loading();
  return bol;
}

// Loops through functions
void loop() {
  int bl = LCDprint();
  if(bl){
    pump_on();
    delay(500);
  }
  Serial.println(lodval);
    
}
